// Logisim project 3B.circ as structural Verilog: 1 circuit, main circuit main
module main (
  input  in_1,
  input  in_2,
  input  in_3,
  input  in_4,
  input  in_5,
  output out_6,
  output out_7,
  output out_8,
  output out_9,
  output out_10,
  output out_11,
  output out_12
);

  wire and_1_out, and_2_out, and_3_out, nand_1_out, or_1_out, or_2_out;

  or or_1 (or_1_out, in_2, in_3);
  or or_2 (or_2_out, out_8, out_9);
  and and_1 (and_1_out, out_10, in_4);
  nand nand_1 (nand_1_out, out_12, in_5);
  not not_1 (out_6, in_1);
  and and_2 (and_2_out, or_1_out, or_2_out);
  and and_3 (and_3_out, and_1_out, nand_1_out);
  not not_2 (out_7, and_2_out);
  or or_3 (out_11, and_3_out, nand_1_out);
endmodule
